// Logisim project Calcrator.circ as structural Verilog
module ALU (
  input  [7:0] IN0,
  input  [7:0] IN1,
  input  [1:0] MODE,
  output [7:0] RESULT,
  output ZERO,
  output NEGATIVE,
  output CARRY
);

  wire adder_1_cout, subtractor_1_bout;
  wire [7:0] adder_1_out, divider_1_out, multiplier_1_out, subtractor_1_out;

  Adder adder_1 (.a(IN0), .b(IN1), .out(adder_1_out), .cout(adder_1_cout));  // open: cin
  Subtractor subtractor_1 (.a(IN0), .b(IN1), .out(subtractor_1_out), .bout(subtractor_1_bout));  // open: bin
  Multiplier multiplier_1 (.a(IN0), .b(IN1), .out(multiplier_1_out));  // open: cin, cout
  Divider divider_1 (.a(IN0), .b(IN1), .out(divider_1_out));  // open: upper, rem
  Multiplexer #(.select(2), .width(8)) multiplexer_1 (
    .in0(adder_1_out), .in1(subtractor_1_out), .in2(multiplier_1_out), .in3(divider_1_out),
    .out({NEGATIVE, RESULT[6:0]}), .sel(MODE));
  Multiplexer #(.select(2)) multiplexer_2 (
    .in0(adder_1_cout), .in1(subtractor_1_bout), .in2(1'b0), .in3(1'b0), .out(CARRY), .sel(MODE));
  Comparator comparator_1 (.a({NEGATIVE, RESULT[6:0]}), .b({8{1'b0}}), .eq(ZERO));  // open: gt, lt

  assign RESULT[7] = NEGATIVE;
endmodule

module regist (
  input  [63:0] DATA_IN,
  input  [2:0] READ_A_SELECT,
  input  [2:0] READ_B_SELECT,
  input  WRITE,
  input  CLOCK,
  input  RESET,
  output [63:0] DATA_A_OUT,
  output [63:0] DATA_B_OUT
);

  wire demultiplexer_2_out0, demultiplexer_2_out1, demultiplexer_2_out2, demultiplexer_2_out3,
       demultiplexer_2_out4, demultiplexer_2_out5, demultiplexer_2_out6, demultiplexer_2_out7;
  wire [63:0] demultiplexer_1_out0, demultiplexer_1_out1, demultiplexer_1_out2, demultiplexer_1_out3,
       demultiplexer_1_out4, demultiplexer_1_out5, demultiplexer_1_out6, demultiplexer_1_out7, R0_q, R1_q,
       R2_q, R3_q, R4_q, R5_q, R6_q, R7_q;

  Demultiplexer #(.select(3), .width(64)) demultiplexer_1 (
    .out0(demultiplexer_1_out0), .out1(demultiplexer_1_out1), .out2(demultiplexer_1_out2),
    .out3(demultiplexer_1_out3), .out4(demultiplexer_1_out4), .out5(demultiplexer_1_out5),
    .out6(demultiplexer_1_out6), .out7(demultiplexer_1_out7), .in(DATA_IN), .sel(READ_A_SELECT));
  Demultiplexer #(.select(3)) demultiplexer_2 (
    .out0(demultiplexer_2_out0), .out1(demultiplexer_2_out1), .out2(demultiplexer_2_out2),
    .out3(demultiplexer_2_out3), .out4(demultiplexer_2_out4), .out5(demultiplexer_2_out5),
    .out6(demultiplexer_2_out6), .out7(demultiplexer_2_out7), .in(WRITE), .sel(READ_A_SELECT));
  Register #(.width(64)) R0 (.D(demultiplexer_1_out0), .en(demultiplexer_2_out0), .clk(CLOCK), .Q(R0_q), .clr(RESET));
  Register #(.width(64)) R1 (.D(demultiplexer_1_out1), .en(demultiplexer_2_out1), .clk(CLOCK), .Q(R1_q), .clr(RESET));
  Register #(.width(64)) R2 (.D(demultiplexer_1_out2), .en(demultiplexer_2_out2), .clk(CLOCK), .Q(R2_q), .clr(RESET));
  Register #(.width(64)) R3 (.D(demultiplexer_1_out3), .en(demultiplexer_2_out3), .clk(CLOCK), .Q(R3_q), .clr(RESET));
  Register #(.width(64)) R4 (.D(demultiplexer_1_out4), .en(demultiplexer_2_out4), .clk(CLOCK), .Q(R4_q), .clr(RESET));
  Register #(.width(64)) R5 (.D(demultiplexer_1_out5), .en(demultiplexer_2_out5), .clk(CLOCK), .Q(R5_q), .clr(RESET));
  Register #(.width(64)) R6 (.D(demultiplexer_1_out6), .en(demultiplexer_2_out6), .clk(CLOCK), .Q(R6_q), .clr(RESET));
  Register #(.width(64)) R7 (.D(demultiplexer_1_out7), .en(demultiplexer_2_out7), .clk(CLOCK), .Q(R7_q), .clr(RESET));
  Multiplexer #(.select(3), .width(64)) multiplexer_1 (
    .in0(R0_q), .in1(R1_q), .in2(R2_q), .in3(R3_q), .in4(R4_q), .in5(R5_q), .in6(R6_q), .in7(R7_q),
    .out(DATA_A_OUT), .sel(READ_A_SELECT));
  Multiplexer #(.select(3), .width(64)) multiplexer_2 (
    .in0(R0_q), .in1(R1_q), .in2(R2_q), .in3(R3_q), .in4(R4_q), .in5(R5_q), .in6(R6_q), .in7(R7_q),
    .out(DATA_B_OUT), .sel(READ_B_SELECT));
endmodule

module CPU (
);

  wire [63:0] pc_1_pc_out;

  ALU alu_1 ();  // open: IN0, IN1, MODE, RESULT, ZERO, NEGATIVE, CARRY
  PC pc_1 (.PC_OUT(pc_1_pc_out));  // open: DATA_IN, LOAD, CLOCK, RESET
  Memory memory_1 (.ADDRESS(pc_1_pc_out[7:0]));  // open: INSTRUCTION
endmodule

module PC (
  input  [63:0] DATA_IN,
  input  LOAD,
  input  CLOCK,
  input  RESET,
  output [63:0] PC_OUT
);

  wire [63:0] adder_1_out, multiplexer_1_out;

  Register #(.width(64)) register_1 (.D(multiplexer_1_out), .clk(CLOCK), .Q(PC_OUT), .clr(RESET));  // open: en
  Adder #(.width(64)) adder_1 (.a(PC_OUT), .b(64'h1), .out(adder_1_out));  // open: cin, cout
  Multiplexer #(.width(64)) multiplexer_1 (.in0(adder_1_out), .in1(DATA_IN), .out(multiplexer_1_out), .sel(LOAD));
endmodule

module Memory (
  input  [7:0] ADDRESS,
  output [15:0] INSTRUCTION
);

  ROM #(.dataWidth(16)) rom_1 (.addr(ADDRESS), .data(INSTRUCTION));

  // Notes on the sheet:
  //   contents of rom_1 (hex, n*v repeats v):
  //   1234 15*0 5678 15*0 abcd 15*0 1111
endmodule

module Decode (
  input  [15:0] INSTRUCTION,
  output [3:0] OPCODE,
  output [2:0] RD,
  output [2:0] RA,
  output [2:0] RB
);


  assign OPCODE = INSTRUCTION[15:12];
  assign RA = INSTRUCTION[8:6];
  assign RB = INSTRUCTION[5:3];
  assign RD = INSTRUCTION[11:9];
endmodule

module ControlUnit (
  input  [3:0] OPCODE,
  output REG_WRITE,
  output [1:0] ALU_OP
);

  wire decoder_1_out1, decoder_1_out2, decoder_1_out3, decoder_1_out4;

  Decoder #(.select(4)) decoder_1 (
    .out1(decoder_1_out1), .out2(decoder_1_out2), .out3(decoder_1_out3), .out4(decoder_1_out4), .sel(OPCODE));  // open: out0, out5, out6, out7, out8, out9, out10, out11, out12, out13, out14, out15, en
  or or_1 (REG_WRITE, decoder_1_out1, decoder_1_out2, decoder_1_out3, decoder_1_out4);
  or or_2 (ALU_OP[0], decoder_1_out2, decoder_1_out4);
  or or_3 (ALU_OP[1], decoder_1_out3, decoder_1_out4);
endmodule
